// Logisim project CPU.circ as structural Verilog: 16 circuits, main circuit main
module main (
  input  in_1,
  input  in_2,
  input  in_3,
  input  in_4,
  output [3:0] Bus_Destination,
  output [3:0] Bus_Source,
  output [11:0] AC,
  output [11:0] PC,
  output [11:0] AR,
  output [11:0] DR,
  output [11:0] TR,
  output [11:0] IX,
  output [17:0] IR,
  output [7:0] INPR,
  output [7:0] OUTR,
  output [17:0] Memory,
  output [11:0] out_17
);

  wire alu_1_cout, and_1_out, and_2_out, and_3_out, and_4_out, and_5_out, and_6_out, and_7_out, and_8_out,
       and_9_out, and_10_out, and_11_out, and_12_out, and_13_out, and_14_out, and_15_out, and_16_out,
       and_17_out, and_18_out, and_19_out, and_20_out, and_21_out, and_22_out, and_23_out, and_24_out,
       and_25_out, and_26_out, and_27_out, and_28_out, and_29_out, and_30_out, and_31_out, and_32_out,
       and_33_out, and_34_out, and_35_out, and_36_out, and_37_out, and_38_out, and_39_out, and_40_out,
       and_41_out, and_42_out, and_43_out, and_44_out, and_45_out, and_46_out, and_47_out, and_48_out,
       and_49_out, and_50_out, and_51_out, and_52_out, and_53_out, and_54_out, and_55_out, and_56_out,
       and_57_out, and_58_out, and_59_out, and_60_out, and_61_out, and_62_out, and_63_out, and_64_out,
       and_65_out, and_66_out, and_67_out, CLK, clock_1_out, D0, D1, D2, D3, D4, D5, D6, D7, D8, D9, D10,
       D11, D12, D13, D14, D15, decoder_1_out0, decoder_1_out1, demultiplexer_1_out0, demultiplexer_1_out1,
       demultiplexer_1_out2, Direct, I, Index, Indirect, n12_bit_negative_1_n, n12_bit_zero_1_out,
       n12_bit_zero_2_out, not_1_out, not_2_out, not_3_out, not_4_out, not_5_out, or_1_out, or_13_out,
       or_14_out, or_15_out, or_16_out, or_17_out, or_18_out, or_19_out, or_20_out, or_24_out, or_25_out,
       or_26_out, or_27_out, or_28_out, or_29_out, or_30_out, or_31_out, or_32_out, or_33_out, or_34_out,
       or_35_out, Overflow, R_q, SC____0_out, T0, T1, T2, T3, T4, T5, T6, T7, T8, T9, T10, T11, T12, T13,
       T14, T15, undriven, xor_1_out;
  wire [1:0] or_2_out, or_21_out;
  wire [2:0] or_6_out, or_9_out;
  wire [7:0] bus_1_inpr_out, bus_1_outr_out;
  wire [11:0] alu_1_d_out, bus_1_ac_out, bus_1_ar_out, bus_1_dr_out, bus_1_ix_out, bus_1_pc_out,
       bus_1_tr_out, demultiplexer_2_out0, demultiplexer_2_out1, multiplexer_1_out, multiplexer_2_out,
       multiplexer_3_out, multiplexer_4_out, n12_bit_and_1_f;
  wire [17:0] bus_1_ir_out, bus_1_m_out;

  Clock clock_1 (.out(clock_1_out));
  assign CLK = xor_1_out ? clock_1_out : 1'bz;  // Controlled_Buffer controlled_buffer_1
  xor xor_1 (xor_1_out, in_1, and_55_out);
  or or_1 (or_1_out, in_2, SC____0_out);
  or SC____0 (SC____0_out, and_61_out, and_59_out, and_6_out, and_57_out, and_54_out, and_52_out, and_50_out, and_48_out, and_46_out, and_44_out, and_42_out, and_40_out, and_38_out, and_36_out, and_33_out, and_29_out, and_25_out, and_23_out, and_21_out, and_19_out, and_16_out);
  Timer timer_1 (
    .Increment(1'b1), .Clock(CLK), .Clear(or_1_out), .T0(T0), .T1(T1), .T2(T2), .T3(T3), .T4(T4), .T5(T5),
    .T6(T6), .T7(T7), .T8(T8), .T9(T9), .T10(T10), .T11(T11), .T12(T12), .T13(T13), .T14(T14), .T15(T15),
    .Overflow(Overflow));
  Instruction_Decoder instruction_decoder_1 (
    ._18_Bit_Input(IR), .Enable(undriven), .Addressing_Mode({I, Index, Indirect, Direct}),
    .Opt_Code({D15, D14, D13, D12, D11, D10, D9, D8, D7, D6, D5, D4, D3, D2, D1, D0}), .Data(out_17));
  Register #(.width(1), .trigger("falling")) R (.D(and_56_out), .en(and_56_out), .Q(R_q), .clk(CLK), .clr(and_6_out));
  Register #(.width(1), .trigger("falling")) E (.D(alu_1_cout), .clk(CLK));  // open: en, Q, clr
  Demultiplexer #(.select(2)) demultiplexer_1 (
    .out0(demultiplexer_1_out0), .out1(demultiplexer_1_out1), .out2(demultiplexer_1_out2), .in(1'b1),
    .sel(out_17[1:0]));  // open: out3, en
  not not_1 (not_1_out, D15);
  Decoder decoder_1 (.out0(decoder_1_out0), .out1(decoder_1_out1), .sel(R_q));  // open: en
  and and_1 (and_1_out, T0, decoder_1_out0);
  and and_2 (and_2_out, T1, decoder_1_out0);
  and and_3 (and_3_out, T2, decoder_1_out0);
  and and_4 (and_4_out, decoder_1_out1, T0);
  and and_5 (and_5_out, decoder_1_out1, T1);
  and and_6 (and_6_out, decoder_1_out1, T2);
  and and_7 (and_7_out, T3, not_1_out, Direct);
  and and_8 (and_8_out, T3, not_1_out, Indirect);
  and and_9 (and_9_out, T3, not_1_out, Index);
  and and_10 (and_10_out, T3, D15, not_2_out);
  not not_2 (not_2_out, I);
  and and_11 (and_11_out, T4, D15, not_3_out);
  not not_3 (not_3_out, I);
  and and_12 (and_12_out, T3, D15, I);
  and and_13 (and_13_out, T4, D15, I);
  and and_14 (and_14_out, T4, D0);
  and and_15 (and_15_out, T5, D0);
  and and_16 (and_16_out, T6, D0);
  and and_17 (and_17_out, T4, D1);
  and and_18 (and_18_out, T5, D1);
  and and_19 (and_19_out, T6, D1);
  and and_20 (and_20_out, T4, D2);
  and and_21 (and_21_out, T5, D2);
  and and_22 (and_22_out, T4, D3);
  and and_23 (and_23_out, T5, D3);
  and and_24 (and_24_out, T4, D4);
  and and_25 (and_25_out, T5, D4);
  and and_26 (and_26_out, T4, D5);
  and and_27 (and_27_out, T5, D5);
  and and_28 (and_28_out, T6, D5);
  and and_29 (and_29_out, T7, D5);
  and and_30 (and_30_out, T4, D6);
  and and_31 (and_31_out, T5, D6);
  and and_32 (and_32_out, T6, D6);
  and and_33 (and_33_out, T7, D6);
  and and_34 (and_34_out, T4, D7);
  and and_35 (and_35_out, T5, D7);
  and and_36 (and_36_out, T6, D7);
  and and_37 (and_37_out, T4, D8);
  and and_38 (and_38_out, T5, D8);
  and and_39 (and_39_out, T4, D9);
  and and_40 (and_40_out, T5, D9);
  and and_41 (and_41_out, T4, D10);
  and and_42 (and_42_out, T5, D10);
  and and_43 (and_43_out, T4, D11);
  and and_44 (and_44_out, T5, D11);
  and and_45 (and_45_out, T4, D12);
  and and_46 (and_46_out, T5, D12);
  and and_47 (and_47_out, T4, D13);
  and and_48 (and_48_out, T5, D13);
  and and_49 (and_49_out, T4, D14);
  and and_50 (and_50_out, T5, D14);
  and and_51 (and_51_out, and_10_out, demultiplexer_1_out0);
  and and_52 (and_52_out, and_11_out, demultiplexer_1_out0);
  and and_53 (and_53_out, and_10_out, demultiplexer_1_out1);
  and and_54 (and_54_out, and_11_out, demultiplexer_1_out1);
  and and_55 (and_55_out, and_10_out, demultiplexer_1_out2);
  and and_56 (and_56_out, and_12_out, demultiplexer_1_out0);
  and and_57 (and_57_out, and_13_out, demultiplexer_1_out0);
  and and_58 (and_58_out, and_12_out, demultiplexer_1_out1);
  and and_59 (and_59_out, and_13_out, demultiplexer_1_out1);
  and and_60 (and_60_out, and_12_out, demultiplexer_1_out2);
  and and_61 (and_61_out, and_13_out, demultiplexer_1_out2);
  buf or_2 (or_2_out[0], and_35_out);  // OR_Gate
  buf or_3 (or_2_out[1], in_3);  // OR_Gate
  ALU alu_1 (
    .Cin(and_35_out), .Selection(or_2_out), .A_In(multiplexer_2_out), .B_In(multiplexer_1_out),
    .D_out(alu_1_d_out), .Cout(alu_1_cout));
  and and_62 (and_62_out, and_47_out, not_5_out);
  and and_63 (and_63_out, and_49_out, n12_bit_negative_1_n);
  Demultiplexer #(.width(12)) demultiplexer_2 (
    .out0(demultiplexer_2_out0), .out1(demultiplexer_2_out1), .in(alu_1_d_out), .sel(and_9_out));  // open: en
  and and_64 (and_64_out, and_62_out, not_4_out);
  and and_65 (and_65_out, and_45_out, not_4_out);
  not not_4 (not_4_out, n12_bit_zero_1_out);
  not not_5 (not_5_out, n12_bit_negative_1_n);
  _12_bit_Negative u_12_bit_negative_1 (.Data(AC), .N(n12_bit_negative_1_n));
  and and_66 (and_66_out, and_43_out, n12_bit_zero_1_out);
  _12_bit_Zero u_12_bit_zero_1 (.IN(AC), .Out(n12_bit_zero_1_out));
  buf or_4 (or_6_out[2], in_4);  // OR_Gate
  or or_5 (or_6_out[1], and_18_out, and_35_out, and_41_out);
  or or_6 (or_6_out[0], in_4, and_41_out);
  or or_7 (or_9_out[2], and_18_out, and_35_out);
  or or_8 (or_9_out[1], and_9_out, in_4);
  or or_9 (or_9_out[0], and_18_out, and_9_out, and_35_out, in_4);
  or or_10 (Bus_Destination[3], and_26_out, and_32_out, and_60_out, and_22_out);
  Multiplexer #(.select(3), .width(12)) multiplexer_1 (
    .in0(IX), .in1(TR), .in2(DR), .in3(AR), .in4(PC), .in5(AC), .out(multiplexer_1_out), .sel(or_6_out));  // open: in6, in7, en
  Multiplexer #(.select(3), .width(12)) multiplexer_2 (
    .in0(IX), .in1(TR), .in2(DR), .in3(AR), .in4(PC), .in5(AC), .out(multiplexer_2_out), .sel(or_9_out));  // open: in6, in7, en
  or or_11 (Bus_Destination[2], and_2_out, and_5_out, and_39_out, and_41_out, and_37_out);
  and and_67 (and_67_out, and_32_out, n12_bit_zero_2_out);
  _12_bit_Zero u_12_bit_zero_2 (.IN(DR), .Out(n12_bit_zero_2_out));
  or or_12 (Bus_Destination[1], and_5_out, and_34_out, and_9_out, and_2_out, and_17_out, and_14_out, and_3_out, and_1_out, and_8_out, and_30_out, and_4_out);
  or or_13 (or_13_out, and_2_out, and_67_out, and_28_out);
  buf or_14 (or_14_out, in_2);  // OR_Gate
  buf or_15 (or_15_out, and_31_out);  // OR_Gate
  buf or_16 (or_16_out, in_2);  // OR_Gate
  buf or_17 (or_17_out, in_2);  // OR_Gate
  buf or_18 (or_18_out, in_2);  // OR_Gate
  buf or_19 (or_19_out, in_2);  // OR_Gate
  buf or_20 (or_20_out, in_2);  // OR_Gate
  or or_21 (or_21_out[0], and_15_out, and_4_out);
  or or_22 (or_21_out[1], and_4_out, and_41_out, and_35_out, and_18_out);
  or or_23 (Bus_Destination[0], and_5_out, and_63_out, and_66_out, and_39_out, and_32_out, and_30_out, and_22_out, and_26_out, and_17_out, and_24_out, and_14_out, and_27_out, and_34_out, and_37_out, and_41_out, and_65_out, and_64_out);
  or or_24 (or_24_out, and_53_out, in_2);
  or or_25 (or_25_out, and_51_out, in_2);
  buf or_26 (or_26_out, in_2);  // OR_Gate
  buf or_27 (or_27_out, in_2);  // OR_Gate
  buf or_28 (or_28_out, in_2);  // OR_Gate
  buf or_29 (or_29_out, in_2);  // OR_Gate
  buf or_30 (or_30_out, in_2);  // OR_Gate
  buf or_31 (or_31_out, in_2);  // OR_Gate
  buf or_32 (or_32_out, in_2);  // OR_Gate
  buf or_33 (or_33_out, in_2);  // OR_Gate
  or or_34 (or_34_out, and_26_out, and_32_out, and_22_out);
  or or_35 (or_35_out, and_4_out, and_20_out, and_2_out, and_8_out, and_17_out, and_30_out, and_14_out, and_34_out, and_37_out, and_5_out);
  Multiplexer #(.width(12)) multiplexer_3 (
    .in0(AR), .in1(demultiplexer_2_out1), .out(multiplexer_3_out), .sel(and_9_out));  // open: en
  or or_36 (Bus_Source[3], and_41_out, and_35_out, and_30_out, and_20_out, and_18_out, and_14_out, and_3_out, and_17_out, and_15_out, and_2_out, and_8_out, and_9_out, and_34_out, and_37_out, and_4_out, and_5_out);
  buf or_37 (Bus_Source[2], and_58_out);  // OR_Gate
  _12_bit_AND u_12_bit_and_1 (.A(AC), .B(DR), .F(n12_bit_and_1_f));
  RAM #(.addrWidth(12), .dataWidth(18), .bus("separate")) ram_1 (
    .addr(multiplexer_3_out), .din(bus_1_m_out), .data(Memory), .str(or_34_out), .clk(CLK), .ld(or_35_out),
    .clr(in_2));  // open: sel
  or or_38 (Bus_Source[1], and_4_out, and_63_out, and_66_out, and_35_out, and_24_out, and_18_out, and_27_out, and_15_out, and_3_out, and_32_out, and_41_out, and_65_out, and_64_out, and_58_out);
  Multiplexer #(.select(2), .width(12)) multiplexer_4 (
    .in0(out_17), .in1(n12_bit_and_1_f), .in2(demultiplexer_2_out0), .in3({12{1'b1}}),
    .out(multiplexer_4_out), .sel(or_21_out));  // open: en
  Register_12bit u_AC (.Increment(or_24_out), .in_2(CLK), .Clear(or_25_out), .Data_In(bus_1_ac_out), .Data_out(AC));
  Register_12bit u_PC (.Increment(or_13_out), .in_2(CLK), .Clear(or_14_out), .Data_In(bus_1_pc_out), .Data_out(PC));
  Register_12bit u_AR (.Increment(or_26_out), .in_2(CLK), .Clear(or_27_out), .Data_In(bus_1_ar_out), .Data_out(AR));
  Register_12bit u_DR (.Increment(or_15_out), .in_2(CLK), .Clear(or_16_out), .Data_In(bus_1_dr_out), .Data_out(DR));
  Register_12bit u_TR (.Increment(or_28_out), .in_2(CLK), .Clear(or_29_out), .Data_In(bus_1_tr_out), .Data_out(TR));
  Register_12bit u_IX (.Increment(or_17_out), .in_2(CLK), .Clear(or_18_out), .Data_In(bus_1_ix_out), .Data_out(IX));
  Register_18bit u_IR (.Increment(or_30_out), .CLK(CLK), .Clear(or_31_out), .Data_In(bus_1_ir_out), .Data_out(IR));
  Register_8bit u_INPR (.Increment(or_19_out), .CLK(CLK), .Clear(or_20_out), .Data_In(bus_1_inpr_out), .Data_out(INPR));
  Register_8bit u_OUTR (.Increment(or_32_out), .CLK(CLK), .Clear(or_33_out), .Data_In(bus_1_outr_out), .Data_out(OUTR));
  or or_39 (Bus_Source[0], and_5_out, and_34_out, and_26_out, and_20_out, and_1_out, and_8_out, and_14_out, and_17_out, and_2_out, and_9_out, and_30_out, and_32_out, and_37_out, and_58_out);
  Bus bus_1 (
    .Source_Selection(Bus_Source), .Destination_Selection(Bus_Destination), .AC_In(AC), .PC_In(PC),
    .AR_in(AR), .DR_In(DR), .TR_In(TR), .IX_in(IX), .IR_in(IR), .INPR(INPR), .OUTR(OUTR), .M_in(Memory),
    .Data_In(multiplexer_4_out), .AC_Out(bus_1_ac_out), .PC_Out(bus_1_pc_out), .AR_Out(bus_1_ar_out),
    .DR_Out(bus_1_dr_out), .TR_Out(bus_1_tr_out), .IX_Out(bus_1_ix_out), .IR_Out(bus_1_ir_out),
    .INPR_Out(bus_1_inpr_out), .OUTR_Out(bus_1_outr_out), .M_Out(bus_1_m_out));

  // Other names for the same wires on the sheet: Reset = in_2

  // Notes on the sheet:
  //   R'  T0
  //   R' T2
  //   R' T1
  //   R T0
  //   R T1
  //   R T2
  //   D15'.D.T3
  //   D15'.In.T3
  //   D15'.X.T3
  //   D15.I'.T3
  //   D15.I'.T4
  //   D15.I.T3
  //   D15.I.T4
  //   T5
  //   T4
  //   T7
  //   T6
  //   Cin
  //   S0
  //   S1
  //   B
  //   A
  //   B
  //   A
  //   Bus Destination
  //   Bus Source
  //   Bus Destination
  //   Bus Source
endmodule

module Timer (
  input  Increment,
  input  Clock,
  input  Clear,
  output T0,
  output T1,
  output T2,
  output T3,
  output T4,
  output T5,
  output T6,
  output T7,
  output T8,
  output T9,
  output T10,
  output T11,
  output T12,
  output T13,
  output T14,
  output T15,
  output Overflow
);

  wire [3:0] counter_1_q;

  Counter #(.width(4), .max('hf), .trigger("falling")) counter_1 (
    .count(Increment), .Q(counter_1_q), .carry(Overflow), .clk(Clock), .clr(Clear));  // open: load, D
  Decoder #(.select(4)) decoder_1 (
    .out0(T0), .out1(T1), .out2(T2), .out3(T3), .out4(T4), .out5(T5), .out6(T6), .out7(T7), .out8(T8),
    .out9(T9), .out10(T10), .out11(T11), .out12(T12), .out13(T13), .out14(T14), .out15(T15), .sel(counter_1_q));  // open: en
endmodule

// ID
module Instruction_Decoder (
  input  [17:0] _18_Bit_Input,
  input  Enable,
  output [3:0] Addressing_Mode,
  output [15:0] Opt_Code,
  output [11:0] Data
);

  Decoder #(.select(2)) decoder_1 (
    .out0(Addressing_Mode[0]), .out1(Addressing_Mode[1]), .out2(Addressing_Mode[2]),
    .out3(Addressing_Mode[3]), .sel(_18_Bit_Input[17:16]), .en(Enable));
  Decoder #(.select(4)) decoder_2 (
    .out0(Opt_Code[0]), .out1(Opt_Code[1]), .out2(Opt_Code[2]), .out3(Opt_Code[3]), .out4(Opt_Code[4]),
    .out5(Opt_Code[5]), .out6(Opt_Code[6]), .out7(Opt_Code[7]), .out8(Opt_Code[8]), .out9(Opt_Code[9]),
    .out10(Opt_Code[10]), .out11(Opt_Code[11]), .out12(Opt_Code[12]), .out13(Opt_Code[13]),
    .out14(Opt_Code[14]), .out15(Opt_Code[15]), .sel(_18_Bit_Input[15:12]), .en(Enable));

  assign Data = _18_Bit_Input[11:0];

  // Other names for the same wires on the sheet: ENB = Enable
endmodule

module Bus (
  input  [3:0] Source_Selection,
  input  [3:0] Destination_Selection,
  input  [11:0] AC_In,
  input  [11:0] PC_In,
  input  [11:0] AR_in,
  input  [11:0] DR_In,
  input  [11:0] TR_In,
  input  [11:0] IX_in,
  input  [17:0] IR_in,
  input  [7:0] INPR,
  input  [7:0] OUTR,
  input  [17:0] M_in,
  input  [11:0] Data_In,
  output [11:0] AC_Out,
  output [11:0] PC_Out,
  output [11:0] AR_Out,
  output [11:0] DR_Out,
  output [11:0] TR_Out,
  output [11:0] IX_Out,
  output [17:0] IR_Out,
  output [7:0] INPR_Out,
  output [7:0] OUTR_Out,
  output [17:0] M_Out
);

  wire decoder_1_out0, decoder_1_out1, decoder_1_out2, decoder_1_out3, decoder_1_out4, decoder_1_out5,
       decoder_1_out6, decoder_1_out7, decoder_1_out8, decoder_1_out9;
  wire [17:0] B, controlled_buffer_1_out, controlled_buffer_2_out, controlled_buffer_3_out,
       controlled_buffer_4_out, controlled_buffer_5_out, controlled_buffer_6_out, controlled_buffer_8_out,
       controlled_buffer_9_out;

  Multiplexer #(.select(4)) multiplexer_1 (
    .in0(AC_In[0]), .in1(PC_In[0]), .in2(AR_in[0]), .in3(DR_In[0]), .in4(TR_In[0]), .in5(IX_in[0]),
    .in6(IR_in[0]), .in7(INPR[0]), .in8(OUTR[0]), .in9(M_in[0]), .in10(Data_In[0]), .out(B[0]),
    .sel(Source_Selection));  // open: in11, in12, in13, in14, in15, en
  Multiplexer #(.select(4)) multiplexer_2 (
    .in0(AC_In[1]), .in1(PC_In[1]), .in2(AR_in[1]), .in3(DR_In[1]), .in4(TR_In[1]), .in5(IX_in[1]),
    .in6(IR_in[1]), .in7(INPR[1]), .in8(OUTR[1]), .in9(M_in[1]), .in10(Data_In[1]), .out(B[1]),
    .sel(Source_Selection));  // open: in11, in12, in13, in14, in15, en
  Multiplexer #(.select(4)) multiplexer_3 (
    .in0(AC_In[2]), .in1(PC_In[2]), .in2(AR_in[2]), .in3(DR_In[2]), .in4(TR_In[2]), .in5(IX_in[2]),
    .in6(IR_in[2]), .in7(INPR[2]), .in8(OUTR[2]), .in9(M_in[2]), .in10(Data_In[2]), .out(B[2]),
    .sel(Source_Selection));  // open: in11, in12, in13, in14, in15, en
  Multiplexer #(.select(4)) multiplexer_4 (
    .in0(AC_In[3]), .in1(PC_In[3]), .in2(AR_in[3]), .in3(DR_In[3]), .in4(TR_In[3]), .in5(IX_in[3]),
    .in6(IR_in[3]), .in7(INPR[3]), .in8(OUTR[3]), .in9(M_in[3]), .in10(Data_In[3]), .out(B[3]),
    .sel(Source_Selection));  // open: in11, in12, in13, in14, in15, en
  Multiplexer #(.select(4)) multiplexer_5 (
    .in0(AC_In[4]), .in1(PC_In[4]), .in2(AR_in[4]), .in3(DR_In[4]), .in4(TR_In[4]), .in5(IX_in[4]),
    .in6(IR_in[4]), .in7(INPR[4]), .in8(OUTR[4]), .in9(M_in[4]), .in10(Data_In[4]), .out(B[4]),
    .sel(Source_Selection));  // open: in11, in12, in13, in14, in15, en
  Multiplexer #(.select(4)) multiplexer_6 (
    .in0(AC_In[5]), .in1(PC_In[5]), .in2(AR_in[5]), .in3(DR_In[5]), .in4(TR_In[5]), .in5(IX_in[5]),
    .in6(IR_in[5]), .in7(INPR[5]), .in8(OUTR[5]), .in9(M_in[5]), .in10(Data_In[5]), .out(B[5]),
    .sel(Source_Selection));  // open: in11, in12, in13, in14, in15, en
  Multiplexer #(.select(4)) multiplexer_7 (
    .in0(AC_In[10]), .in1(PC_In[10]), .in2(AR_in[10]), .in3(DR_In[10]), .in4(TR_In[10]), .in5(IX_in[10]),
    .in6(IR_in[10]), .in7(1'b0), .in8(1'b0), .in9(M_in[10]), .in10(Data_In[10]), .out(B[10]),
    .sel(Source_Selection));  // open: in11, in12, in13, in14, in15, en
  Multiplexer #(.select(4)) multiplexer_8 (
    .in0(AC_In[11]), .in1(PC_In[11]), .in2(AR_in[11]), .in3(DR_In[11]), .in4(TR_In[11]), .in5(IX_in[11]),
    .in6(IR_in[11]), .in7(1'b0), .in8(1'b0), .in9(M_in[11]), .in10(Data_In[11]), .out(B[11]),
    .sel(Source_Selection));  // open: in11, in12, in13, in14, in15, en
  Multiplexer #(.select(4)) multiplexer_9 (
    .in0(AC_In[6]), .in1(PC_In[6]), .in2(AR_in[6]), .in3(DR_In[6]), .in4(TR_In[6]), .in5(IX_in[6]),
    .in6(IR_in[6]), .in7(INPR[6]), .in8(OUTR[6]), .in9(M_in[6]), .in10(Data_In[6]), .out(B[6]),
    .sel(Source_Selection));  // open: in11, in12, in13, in14, in15, en
  Multiplexer #(.select(4)) multiplexer_10 (
    .in0(AC_In[7]), .in1(PC_In[7]), .in2(AR_in[7]), .in3(DR_In[7]), .in4(TR_In[7]), .in5(IX_in[7]),
    .in6(IR_in[7]), .in7(INPR[7]), .in8(OUTR[7]), .in9(M_in[7]), .in10(Data_In[7]), .out(B[7]),
    .sel(Source_Selection));  // open: in11, in12, in13, in14, in15, en
  Multiplexer #(.select(4)) multiplexer_11 (
    .in0(AC_In[8]), .in1(PC_In[8]), .in2(AR_in[8]), .in3(DR_In[8]), .in4(TR_In[8]), .in5(IX_in[8]),
    .in6(IR_in[8]), .in7(1'b0), .in8(1'b0), .in9(M_in[8]), .in10(Data_In[8]), .out(B[8]),
    .sel(Source_Selection));  // open: in11, in12, in13, in14, in15, en
  Multiplexer #(.select(4)) multiplexer_12 (
    .in0(AC_In[9]), .in1(PC_In[9]), .in2(AR_in[9]), .in3(DR_In[9]), .in4(TR_In[9]), .in5(IX_in[9]),
    .in6(IR_in[9]), .in7(1'b0), .in8(1'b0), .in9(M_in[9]), .in10(Data_In[9]), .out(B[9]),
    .sel(Source_Selection));  // open: in11, in12, in13, in14, in15, en
  Multiplexer #(.select(4)) multiplexer_13 (
    .in0(1'b0), .in1(1'b0), .in2(1'b0), .in3(1'b0), .in4(1'b0), .in5(1'b0), .in6(IR_in[13]), .in7(1'b0),
    .in8(1'b0), .in9(M_in[13]), .out(B[13]), .sel(Source_Selection));  // open: in10, in11, in12, in13, in14, in15, en
  Multiplexer #(.select(4)) multiplexer_14 (
    .in0(1'b0), .in1(1'b0), .in2(1'b0), .in3(1'b0), .in4(1'b0), .in5(1'b0), .in6(IR_in[14]), .in7(1'b0),
    .in8(1'b0), .in9(M_in[14]), .out(B[14]), .sel(Source_Selection));  // open: in10, in11, in12, in13, in14, in15, en
  Multiplexer #(.select(4)) multiplexer_15 (
    .in0(1'b0), .in1(1'b0), .in2(1'b0), .in3(1'b0), .in4(1'b0), .in5(1'b0), .in6(IR_in[15]), .in7(1'b0),
    .in8(1'b0), .in9(M_in[15]), .out(B[15]), .sel(Source_Selection));  // open: in10, in11, in12, in13, in14, in15, en
  Multiplexer #(.select(4)) multiplexer_16 (
    .in0(1'b0), .in1(1'b0), .in2(1'b0), .in3(1'b0), .in4(1'b0), .in5(1'b0), .in6(IR_in[16]), .in7(1'b0),
    .in8(1'b0), .in9(M_in[16]), .out(B[16]), .sel(Source_Selection));  // open: in10, in11, in12, in13, in14, in15, en
  Multiplexer #(.select(4)) multiplexer_17 (
    .in0(1'b0), .in1(1'b0), .in2(1'b0), .in3(1'b0), .in4(1'b0), .in5(1'b0), .in6(IR_in[17]), .in7(1'b0),
    .in8(1'b0), .in9(M_in[17]), .out(B[17]), .sel(Source_Selection));  // open: in10, in11, in12, in13, in14, in15, en
  Multiplexer #(.select(4)) multiplexer_18 (
    .in0(1'b0), .in1(1'b0), .in2(1'b0), .in3(1'b0), .in4(1'b0), .in5(1'b0), .in6(IR_in[12]), .in7(1'b0),
    .in8(1'b0), .in9(M_in[12]), .out(B[12]), .sel(Source_Selection));  // open: in10, in11, in12, in13, in14, in15, en
  Decoder #(.select(4)) decoder_1 (
    .out0(decoder_1_out0), .out1(decoder_1_out1), .out2(decoder_1_out2), .out3(decoder_1_out3),
    .out4(decoder_1_out4), .out5(decoder_1_out5), .out6(decoder_1_out6), .out7(decoder_1_out7),
    .out8(decoder_1_out8), .out9(decoder_1_out9), .sel(Destination_Selection));  // open: out10, out11, out12, out13, out14, out15, en
  assign controlled_buffer_1_out = decoder_1_out0 ? B : 18'bz;  // Controlled_Buffer controlled_buffer_1
  assign controlled_buffer_2_out = decoder_1_out1 ? B : 18'bz;  // Controlled_Buffer controlled_buffer_2
  assign controlled_buffer_3_out = decoder_1_out2 ? B : 18'bz;  // Controlled_Buffer controlled_buffer_3
  assign controlled_buffer_4_out = decoder_1_out3 ? B : 18'bz;  // Controlled_Buffer controlled_buffer_4
  assign controlled_buffer_5_out = decoder_1_out4 ? B : 18'bz;  // Controlled_Buffer controlled_buffer_5
  assign controlled_buffer_6_out = decoder_1_out5 ? B : 18'bz;  // Controlled_Buffer controlled_buffer_6
  assign IR_Out = decoder_1_out6 ? B : 18'bz;  // Controlled_Buffer controlled_buffer_7
  assign controlled_buffer_8_out = decoder_1_out7 ? B : 18'bz;  // Controlled_Buffer controlled_buffer_8
  assign controlled_buffer_9_out = decoder_1_out8 ? B : 18'bz;  // Controlled_Buffer controlled_buffer_9
  assign M_Out = decoder_1_out9 ? B : 18'bz;  // Controlled_Buffer controlled_buffer_10
  _18B212B u_18b212b_1 (._12b_Output(AC_Out), ._18b_input(controlled_buffer_1_out));
  _18B212B u_18b212b_2 (._12b_Output(PC_Out), ._18b_input(controlled_buffer_2_out));
  _18B212B u_18b212b_3 (._12b_Output(AR_Out), ._18b_input(controlled_buffer_3_out));
  _18B212B u_18b212b_4 (._12b_Output(DR_Out), ._18b_input(controlled_buffer_4_out));
  _18B212B u_18b212b_5 (._12b_Output(TR_Out), ._18b_input(controlled_buffer_5_out));
  _18B212B u_18b212b_6 (._12b_Output(IX_Out), ._18b_input(controlled_buffer_6_out));
  _18B28B u_18b28b_1 (._8b_Output(INPR_Out), ._18b_input(controlled_buffer_8_out));
  _18B28B u_18b28b_2 (._8b_Output(OUTR_Out), ._18b_input(controlled_buffer_9_out));

  // Other names for the same wires on the sheet: AC0 = AC_In[0]; AC1 = AC_In[1]; AC2 = AC_In[2]; AC3 = AC_In[3];
  //   AC4 = AC_In[4]; AC5 = AC_In[5]; AC6 = AC_In[6]; AC7 = AC_In[7]; AC8 = AC_In[8]; AC9 = AC_In[9];
  //   AC10 = AC_In[10]; AC11 = AC_In[11]; AR0 = AR_in[0]; AR1 = AR_in[1]; AR2 = AR_in[2]; AR3 = AR_in[3];
  //   AR4 = AR_in[4]; AR5 = AR_in[5]; AR6 = AR_in[6]; AR7 = AR_in[7]; AR8 = AR_in[8]; AR9 = AR_in[9];
  //   AR10 = AR_in[10]; AR11 = AR_in[11]; D0 = Data_In[0]; D1 = Data_In[1]; D2 = Data_In[2]; D3 = Data_In[3];
  //   D4 = Data_In[4]; D5 = Data_In[5]; D6 = Data_In[6]; D7 = Data_In[7]; D8 = Data_In[8]; D9 = Data_In[9];
  //   D10 = Data_In[10]; D11 = Data_In[11]; DR0 = DR_In[0]; DR1 = DR_In[1]; DR2 = DR_In[2]; DR3 = DR_In[3];
  //   DR4 = DR_In[4]; DR5 = DR_In[5]; DR6 = DR_In[6]; DR7 = DR_In[7]; DR8 = DR_In[8]; DR9 = DR_In[9];
  //   DR10 = DR_In[10]; DR11 = DR_In[11]; DS[3:0] = Destination_Selection; IR0 = IR_in[0]; IR1 = IR_in[1];
  //   IR2 = IR_in[2]; IR3 = IR_in[3]; IR4 = IR_in[4]; IR5 = IR_in[5]; IR6 = IR_in[6]; IR7 = IR_in[7]; IR8 = IR_in[8];
  //   IR9 = IR_in[9]; IR10 = IR_in[10]; IR11 = IR_in[11]; IR12 = IR_in[12]; IR13 = IR_in[13]; IR14 = IR_in[14];
  //   IR15 = IR_in[15]; IR16 = IR_in[16]; IR17 = IR_in[17]; IX0 = IX_in[0]; IX1 = IX_in[1]; IX2 = IX_in[2];
  //   IX3 = IX_in[3]; IX4 = IX_in[4]; IX5 = IX_in[5]; IX6 = IX_in[6]; IX7 = IX_in[7]; IX8 = IX_in[8]; IX9 = IX_in[9];
  //   IX10 = IX_in[10]; IX11 = IX_in[11]; M0 = M_in[0]; M1 = M_in[1]; M2 = M_in[2]; M3 = M_in[3]; M4 = M_in[4];
  //   M5 = M_in[5]; M6 = M_in[6]; M7 = M_in[7]; M8 = M_in[8]; M9 = M_in[9]; M10 = M_in[10]; M11 = M_in[11];
  //   M12 = M_in[12]; M13 = M_in[13]; M14 = M_in[14]; M15 = M_in[15]; M16 = M_in[16]; M17 = M_in[17]; PC0 = PC_In[0];
  //   PC1 = PC_In[1]; PC2 = PC_In[2]; PC3 = PC_In[3]; PC4 = PC_In[4]; PC5 = PC_In[5]; PC6 = PC_In[6]; PC7 = PC_In[7];
  //   PC8 = PC_In[8]; PC9 = PC_In[9]; PC10 = PC_In[10]; PC11 = PC_In[11]; SS[3:0] = Source_Selection; TR0 = TR_In[0];
  //   TR1 = TR_In[1]; TR2 = TR_In[2]; TR3 = TR_In[3]; TR4 = TR_In[4]; TR5 = TR_In[5]; TR6 = TR_In[6]; TR7 = TR_In[7];
  //   TR8 = TR_In[8]; TR9 = TR_In[9]; TR10 = TR_In[10]; TR11 = TR_In[11]
endmodule

module _18B212B (
  input  [17:0] _18b_input,
  output [11:0] _12b_Output
);


  assign _12b_Output = _18b_input[11:0];

  // Notes on the sheet:
  //   TODO: Manage orientation of these lines
endmodule

module _12B218B (
  input  [11:0] _12b_Input,
  output [17:0] _18b_output
);


  assign _18b_output = {{6{1'b0}}, _12b_Input};

  // Notes on the sheet:
  //   TODO: Manage orientation of these lines
endmodule

module Memory (
  input  [17:0] in_1,
  input  in_2,
  input  [11:0] in_3,
  input  [1:0] in_4,
  input  in_5,
  input  [1:0] in_6,
  input  in_7,
  input  in_8
);

  wire clock_1_out;

  RAM #(.addrWidth(12), .dataWidth(18)) ram_1 (
    .addr(in_3), .data(in_1), .clk(clock_1_out), .ld(in_2));  // open: sel, clr
  Clock clock_1 (.out(clock_1_out));
  RAM #(.addrWidth(2), .dataWidth(2), .bus("asynch")) ram_2 (.addr(in_4), .sel(in_7), .ld(in_8));  // open: data, clr
endmodule

module _18B28B (
  input  [17:0] _18b_input,
  output [7:0] _8b_Output
);


  assign _8b_Output = _18b_input[7:0];

  // Notes on the sheet:
  //   TODO: Manage orientation of these lines
endmodule

module test (
  input  [17:0] in_1,
  input  in_2,
  input  in_3,
  input  in_4,
  input  [3:0] in_5,
  output [17:0] out_6
);

  wire and_1_out, and_2_out, and_3_out, B0, B1, B2, B3, B4, B5, B6, B7, B8, B9, B10, B11, clock_1_out, D15,
       I0, I1, I2, I3, not_1_out, T3;
  wire [14:0] instruction_decoder_1_opt_code;

  RAM #(.addrWidth(16), .dataWidth(18)) ram_1 ();  // open: addr, data, sel, clk, ld, clr
  Clock clock_1 (.out(clock_1_out));
  Timer timer_1 (
    .Clock(clock_1_out), .T3(T3));  // open: Increment, Clear, T0, T1, T2, T4, T5, T6, T7, T8, T9, T10, T11, T12, T13, T14, T15, Overflow
  // Bus bus_1: pin names not known; wires that end beside it: in_3, in_3, in_3, in_4, clock_1_out, in_5, in_1, in_3, in_4, clock_1_out, in_5, out_6
  Instruction_Decoder instruction_decoder_1 (
    ._18_Bit_Input(in_1), .Enable(in_2), .Addressing_Mode({I3, I2, I1, I0}),
    .Opt_Code({D15, instruction_decoder_1_opt_code}),
    .Data({B11, B10, B9, B8, B7, B6, B5, B4, B3, B2, B1, B0}));
  and and_1 (and_1_out, I0, D15, T3);
  not not_1 (not_1_out, and_2_out);
  and and_2 (and_2_out, B0, B1, B2, B3, B4, B5, B6, B7, B8, B9, B10, B11);
  and and_3 (and_3_out, and_1_out, not_1_out);
  Register #(.width(12)) Accumulator (.clr(and_3_out));  // open: D, en, Q, clk
endmodule

module ALU (
  input  Cin,
  input  [1:0] Selection,
  input  [11:0] A_In,
  input  [11:0] B_In,
  output [11:0] D_out,
  output Cout
);

  wire adder_1_cout, adder_2_cout, adder_3_cout, adder_4_cout, adder_5_cout, adder_6_cout, adder_7_cout,
       adder_8_cout, adder_9_cout, adder_10_cout, adder_11_cout, multiplexer_1_out, multiplexer_2_out,
       multiplexer_3_out, multiplexer_4_out, multiplexer_5_out, multiplexer_6_out, multiplexer_7_out,
       multiplexer_8_out, multiplexer_9_out, multiplexer_10_out, multiplexer_11_out, multiplexer_12_out,
       not_1_out, not_2_out, not_3_out, not_4_out, not_5_out, not_6_out, not_7_out, not_8_out, not_9_out,
       not_10_out, not_11_out, not_12_out, not_13_out, not_14_out, not_15_out, not_16_out, not_17_out,
       not_18_out, not_19_out, not_20_out, not_21_out, not_22_out, not_23_out, not_24_out;

  not not_1 (not_1_out, B_In[0]);
  not not_2 (not_2_out, 1'b0);
  not not_3 (not_3_out, B_In[1]);
  not not_4 (not_4_out, 1'b0);
  not not_5 (not_5_out, B_In[2]);
  not not_6 (not_6_out, 1'b0);
  not not_7 (not_7_out, B_In[3]);
  not not_8 (not_8_out, 1'b0);
  not not_9 (not_9_out, B_In[4]);
  not not_10 (not_10_out, 1'b0);
  not not_11 (not_11_out, B_In[5]);
  not not_12 (not_12_out, 1'b0);
  not not_13 (not_13_out, B_In[6]);
  not not_14 (not_14_out, 1'b0);
  not not_15 (not_15_out, B_In[7]);
  not not_16 (not_16_out, 1'b0);
  not not_17 (not_17_out, B_In[8]);
  not not_18 (not_18_out, 1'b0);
  not not_19 (not_19_out, B_In[9]);
  not not_20 (not_20_out, 1'b0);
  not not_21 (not_21_out, B_In[10]);
  not not_22 (not_22_out, 1'b0);
  not not_23 (not_23_out, B_In[11]);
  not not_24 (not_24_out, 1'b0);
  Multiplexer #(.select(2)) multiplexer_1 (
    .in0(B_In[0]), .in1(not_1_out), .in2(1'b0), .in3(not_2_out), .out(multiplexer_1_out), .sel(Selection));  // open: en
  Multiplexer #(.select(2)) multiplexer_2 (
    .in0(B_In[1]), .in1(not_3_out), .in2(1'b0), .in3(not_4_out), .out(multiplexer_2_out), .sel(Selection));  // open: en
  Multiplexer #(.select(2)) multiplexer_3 (
    .in0(B_In[2]), .in1(not_5_out), .in2(1'b0), .in3(not_6_out), .out(multiplexer_3_out), .sel(Selection));  // open: en
  Multiplexer #(.select(2)) multiplexer_4 (
    .in0(B_In[3]), .in1(not_7_out), .in2(1'b0), .in3(not_8_out), .out(multiplexer_4_out), .sel(Selection));  // open: en
  Multiplexer #(.select(2)) multiplexer_5 (
    .in0(B_In[4]), .in1(not_9_out), .in2(1'b0), .in3(not_10_out), .out(multiplexer_5_out), .sel(Selection));  // open: en
  Multiplexer #(.select(2)) multiplexer_6 (
    .in0(B_In[5]), .in1(not_11_out), .in2(1'b0), .in3(not_12_out), .out(multiplexer_6_out), .sel(Selection));  // open: en
  Multiplexer #(.select(2)) multiplexer_7 (
    .in0(B_In[6]), .in1(not_13_out), .in2(1'b0), .in3(not_14_out), .out(multiplexer_7_out), .sel(Selection));  // open: en
  Multiplexer #(.select(2)) multiplexer_8 (
    .in0(B_In[7]), .in1(not_15_out), .in2(1'b0), .in3(not_16_out), .out(multiplexer_8_out), .sel(Selection));  // open: en
  Multiplexer #(.select(2)) multiplexer_9 (
    .in0(B_In[8]), .in1(not_17_out), .in2(1'b0), .in3(not_18_out), .out(multiplexer_9_out), .sel(Selection));  // open: en
  Multiplexer #(.select(2)) multiplexer_10 (
    .in0(B_In[9]), .in1(not_19_out), .in2(1'b0), .in3(not_20_out), .out(multiplexer_10_out), .sel(Selection));  // open: en
  Multiplexer #(.select(2)) multiplexer_11 (
    .in0(B_In[10]), .in1(not_21_out), .in2(1'b0), .in3(not_22_out), .out(multiplexer_11_out), .sel(Selection));  // open: en
  Multiplexer #(.select(2)) multiplexer_12 (
    .in0(B_In[11]), .in1(not_23_out), .in2(1'b0), .in3(not_24_out), .out(multiplexer_12_out), .sel(Selection));  // open: en
  Adder #(.width(1)) adder_1 (.a(A_In[0]), .b(multiplexer_1_out), .out(D_out[0]), .cin(Cin), .cout(adder_1_cout));
  Adder #(.width(1)) adder_2 (
    .a(A_In[1]), .b(multiplexer_2_out), .out(D_out[1]), .cin(adder_1_cout), .cout(adder_2_cout));
  Adder #(.width(1)) adder_3 (
    .a(A_In[2]), .b(multiplexer_3_out), .out(D_out[2]), .cin(adder_2_cout), .cout(adder_3_cout));
  Adder #(.width(1)) adder_4 (
    .a(A_In[3]), .b(multiplexer_4_out), .out(D_out[3]), .cin(adder_3_cout), .cout(adder_4_cout));
  Adder #(.width(1)) adder_5 (
    .a(A_In[4]), .b(multiplexer_5_out), .out(D_out[4]), .cin(adder_4_cout), .cout(adder_5_cout));
  Adder #(.width(1)) adder_6 (
    .a(A_In[5]), .b(multiplexer_6_out), .out(D_out[5]), .cin(adder_5_cout), .cout(adder_6_cout));
  Adder #(.width(1)) adder_7 (
    .a(A_In[6]), .b(multiplexer_7_out), .out(D_out[6]), .cin(adder_6_cout), .cout(adder_7_cout));
  Adder #(.width(1)) adder_8 (
    .a(A_In[7]), .b(multiplexer_8_out), .out(D_out[7]), .cin(adder_7_cout), .cout(adder_8_cout));
  Adder #(.width(1)) adder_9 (
    .a(A_In[8]), .b(multiplexer_9_out), .out(D_out[8]), .cin(adder_8_cout), .cout(adder_9_cout));
  Adder #(.width(1)) adder_10 (
    .a(A_In[9]), .b(multiplexer_10_out), .out(D_out[9]), .cin(adder_9_cout), .cout(adder_10_cout));
  Adder #(.width(1)) adder_11 (
    .a(A_In[10]), .b(multiplexer_11_out), .out(D_out[10]), .cin(adder_10_cout), .cout(adder_11_cout));
  Adder #(.width(1)) adder_12 (.a(A_In[11]), .b(multiplexer_12_out), .out(D_out[11]), .cin(adder_11_cout), .cout(Cout));

  // Other names for the same wires on the sheet: A0 = A_In[0]; A1 = A_In[1]; A2 = A_In[2]; A3 = A_In[3]; A4 = A_In[4];
  //   A5 = A_In[5]; A6 = A_In[6]; A7 = A_In[7]; A8 = A_In[8]; A9 = A_In[9]; A10 = A_In[10]; A11 = A_In[11];
  //   B0 = B_In[0]; B1 = B_In[1]; B2 = B_In[2]; B3 = B_In[3]; B4 = B_In[4]; B5 = B_In[5]; B6 = B_In[6]; B7 = B_In[7];
  //   B8 = B_In[8]; B9 = B_In[9]; B10 = B_In[10]; B11 = B_In[11]; C = Cin; S[1:0] = Selection
endmodule

// R12
module Register_12bit (
  input  Increment,
  input  in_2,
  input  Clear,
  input  [11:0] Data_In,
  output [11:0] Data_out
);

  wire [11:0] adder_1_out, controlled_buffer_1_out, multiplexer_1_out;

  Multiplexer #(.width(12)) multiplexer_1 (
    .in0(Data_In), .in1(adder_1_out), .out(multiplexer_1_out), .sel(Increment));  // open: en
  D_Flip_Flop #(.trigger("falling")) d_ff_1 (
    .clk(in_2), .D(multiplexer_1_out[11]), .Q(Data_out[11]), .reset(Clear));  // open: Qn, preset, en
  D_Flip_Flop #(.trigger("falling")) d_ff_2 (
    .clk(in_2), .D(multiplexer_1_out[10]), .Q(Data_out[10]), .reset(Clear));  // open: Qn, preset, en
  D_Flip_Flop #(.trigger("falling")) d_ff_3 (
    .clk(in_2), .D(multiplexer_1_out[9]), .Q(Data_out[9]), .reset(Clear));  // open: Qn, preset, en
  D_Flip_Flop #(.trigger("falling")) d_ff_4 (
    .clk(in_2), .D(multiplexer_1_out[8]), .Q(Data_out[8]), .reset(Clear));  // open: Qn, preset, en
  D_Flip_Flop #(.trigger("falling")) d_ff_5 (
    .clk(in_2), .D(multiplexer_1_out[7]), .Q(Data_out[7]), .reset(Clear));  // open: Qn, preset, en
  D_Flip_Flop #(.trigger("falling")) d_ff_6 (
    .clk(in_2), .D(multiplexer_1_out[6]), .Q(Data_out[6]), .reset(Clear));  // open: Qn, preset, en
  D_Flip_Flop #(.trigger("falling")) d_ff_7 (
    .clk(in_2), .D(multiplexer_1_out[5]), .Q(Data_out[5]), .reset(Clear));  // open: Qn, preset, en
  D_Flip_Flop #(.trigger("falling")) d_ff_8 (
    .clk(in_2), .D(multiplexer_1_out[4]), .Q(Data_out[4]), .reset(Clear));  // open: Qn, preset, en
  D_Flip_Flop #(.trigger("falling")) d_ff_9 (
    .clk(in_2), .D(multiplexer_1_out[3]), .Q(Data_out[3]), .reset(Clear));  // open: Qn, preset, en
  D_Flip_Flop #(.trigger("falling")) d_ff_10 (
    .clk(in_2), .D(multiplexer_1_out[2]), .Q(Data_out[2]), .reset(Clear));  // open: Qn, preset, en
  D_Flip_Flop #(.trigger("falling")) d_ff_11 (
    .clk(in_2), .D(multiplexer_1_out[1]), .Q(Data_out[1]), .reset(Clear));  // open: Qn, preset, en
  D_Flip_Flop #(.trigger("falling")) d_ff_12 (
    .clk(in_2), .D(multiplexer_1_out[0]), .Q(Data_out[0]), .reset(Clear));  // open: Qn, preset, en
  assign controlled_buffer_1_out = Increment ? Data_out : 12'bz;  // Controlled_Buffer controlled_buffer_1
  Adder #(.width(12)) adder_1 (
    .a(controlled_buffer_1_out), .b({12{1'b0}}), .out(adder_1_out), .cin(1'b1));  // open: cout
endmodule

// R18
module Register_18bit (
  input  Increment,
  input  CLK,
  input  Clear,
  input  [17:0] Data_In,
  output [17:0] Data_out
);

  wire [17:0] adder_1_out, controlled_buffer_1_out, multiplexer_1_out;

  Multiplexer #(.width(18)) multiplexer_1 (
    .in0(Data_In), .in1(adder_1_out), .out(multiplexer_1_out), .sel(Increment));  // open: en
  D_Flip_Flop #(.trigger("falling")) d_ff_1 (
    .clk(CLK), .D(multiplexer_1_out[17]), .Q(Data_out[17]), .reset(Clear));  // open: Qn, preset, en
  D_Flip_Flop #(.trigger("falling")) d_ff_2 (
    .clk(CLK), .D(multiplexer_1_out[16]), .Q(Data_out[16]), .reset(Clear));  // open: Qn, preset, en
  D_Flip_Flop #(.trigger("falling")) d_ff_3 (
    .clk(CLK), .D(multiplexer_1_out[15]), .Q(Data_out[15]), .reset(Clear));  // open: Qn, preset, en
  D_Flip_Flop #(.trigger("falling")) d_ff_4 (
    .clk(CLK), .D(multiplexer_1_out[14]), .Q(Data_out[14]), .reset(Clear));  // open: Qn, preset, en
  D_Flip_Flop #(.trigger("falling")) d_ff_5 (
    .clk(CLK), .D(multiplexer_1_out[13]), .Q(Data_out[13]), .reset(Clear));  // open: Qn, preset, en
  D_Flip_Flop #(.trigger("falling")) d_ff_6 (
    .clk(CLK), .D(multiplexer_1_out[12]), .Q(Data_out[12]), .reset(Clear));  // open: Qn, preset, en
  D_Flip_Flop #(.trigger("falling")) d_ff_7 (
    .clk(CLK), .D(multiplexer_1_out[11]), .Q(Data_out[11]), .reset(Clear));  // open: Qn, preset, en
  D_Flip_Flop #(.trigger("falling")) d_ff_8 (
    .clk(CLK), .D(multiplexer_1_out[10]), .Q(Data_out[10]), .reset(Clear));  // open: Qn, preset, en
  D_Flip_Flop #(.trigger("falling")) d_ff_9 (
    .clk(CLK), .D(multiplexer_1_out[9]), .Q(Data_out[9]), .reset(Clear));  // open: Qn, preset, en
  D_Flip_Flop #(.trigger("falling")) d_ff_10 (
    .clk(CLK), .D(multiplexer_1_out[8]), .Q(Data_out[8]), .reset(Clear));  // open: Qn, preset, en
  D_Flip_Flop #(.trigger("falling")) d_ff_11 (
    .clk(CLK), .D(multiplexer_1_out[7]), .Q(Data_out[7]), .reset(Clear));  // open: Qn, preset, en
  D_Flip_Flop #(.trigger("falling")) d_ff_12 (
    .clk(CLK), .D(multiplexer_1_out[6]), .Q(Data_out[6]), .reset(Clear));  // open: Qn, preset, en
  D_Flip_Flop #(.trigger("falling")) d_ff_13 (
    .clk(CLK), .D(multiplexer_1_out[5]), .Q(Data_out[5]), .reset(Clear));  // open: Qn, preset, en
  D_Flip_Flop #(.trigger("falling")) d_ff_14 (
    .clk(CLK), .D(multiplexer_1_out[4]), .Q(Data_out[4]), .reset(Clear));  // open: Qn, preset, en
  D_Flip_Flop #(.trigger("falling")) d_ff_15 (
    .clk(CLK), .D(multiplexer_1_out[3]), .Q(Data_out[3]), .reset(Clear));  // open: Qn, preset, en
  D_Flip_Flop #(.trigger("falling")) d_ff_16 (
    .clk(CLK), .D(multiplexer_1_out[2]), .Q(Data_out[2]), .reset(Clear));  // open: Qn, preset, en
  D_Flip_Flop #(.trigger("falling")) d_ff_17 (
    .clk(CLK), .D(multiplexer_1_out[1]), .Q(Data_out[1]), .reset(Clear));  // open: Qn, preset, en
  D_Flip_Flop #(.trigger("falling")) d_ff_18 (
    .clk(CLK), .D(multiplexer_1_out[0]), .Q(Data_out[0]), .reset(Clear));  // open: Qn, preset, en
  assign controlled_buffer_1_out = Increment ? Data_out : 18'bz;  // Controlled_Buffer controlled_buffer_1
  Adder #(.width(18)) adder_1 (
    .a(controlled_buffer_1_out), .b({18{1'b0}}), .out(adder_1_out), .cin(1'b1));  // open: cout
endmodule

// R8
module Register_8bit (
  input  Increment,
  input  CLK,
  input  Clear,
  input  [7:0] Data_In,
  output [7:0] Data_out
);

  wire [7:0] adder_1_out, controlled_buffer_1_out, multiplexer_1_out;

  Multiplexer #(.width(8)) multiplexer_1 (
    .in0(Data_In), .in1(adder_1_out), .out(multiplexer_1_out), .sel(Increment));  // open: en
  D_Flip_Flop #(.trigger("falling")) d_ff_1 (
    .clk(CLK), .D(multiplexer_1_out[7]), .Q(Data_out[7]), .reset(Clear));  // open: Qn, preset, en
  D_Flip_Flop #(.trigger("falling")) d_ff_2 (
    .clk(CLK), .D(multiplexer_1_out[6]), .Q(Data_out[6]), .reset(Clear));  // open: Qn, preset, en
  D_Flip_Flop #(.trigger("falling")) d_ff_3 (
    .clk(CLK), .D(multiplexer_1_out[5]), .Q(Data_out[5]), .reset(Clear));  // open: Qn, preset, en
  D_Flip_Flop #(.trigger("falling")) d_ff_4 (
    .clk(CLK), .D(multiplexer_1_out[4]), .Q(Data_out[4]), .reset(Clear));  // open: Qn, preset, en
  D_Flip_Flop #(.trigger("falling")) d_ff_5 (
    .clk(CLK), .D(multiplexer_1_out[3]), .Q(Data_out[3]), .reset(Clear));  // open: Qn, preset, en
  D_Flip_Flop #(.trigger("falling")) d_ff_6 (
    .clk(CLK), .D(multiplexer_1_out[2]), .Q(Data_out[2]), .reset(Clear));  // open: Qn, preset, en
  D_Flip_Flop #(.trigger("falling")) d_ff_7 (
    .clk(CLK), .D(multiplexer_1_out[1]), .Q(Data_out[1]), .reset(Clear));  // open: Qn, preset, en
  D_Flip_Flop #(.trigger("falling")) d_ff_8 (
    .clk(CLK), .D(multiplexer_1_out[0]), .Q(Data_out[0]), .reset(Clear));  // open: Qn, preset, en
  assign controlled_buffer_1_out = Increment ? Data_out : 8'bz;  // Controlled_Buffer controlled_buffer_1
  Adder adder_1 (.a(controlled_buffer_1_out), .b({8{1'b0}}), .out(adder_1_out), .cin(1'b1));  // open: cout
endmodule

// AND
module _12_bit_AND (
  input  [11:0] A,
  input  [11:0] B,
  output [11:0] F
);

  and and_1 (F[0], A[0], B[0]);
  and and_2 (F[1], A[1], B[1]);
  and and_3 (F[2], A[2], B[2]);
  and and_4 (F[3], A[3], B[3]);
  and and_5 (F[4], A[4], B[4]);
  and and_6 (F[5], A[5], B[5]);
  and and_7 (F[6], A[6], B[6]);
  and and_8 (F[7], A[7], B[7]);
  and and_9 (F[8], A[8], B[8]);
  and and_10 (F[9], A[9], B[9]);
  and and_11 (F[10], A[10], B[10]);
  and and_12 (F[11], A[11], B[11]);
endmodule

// Zero
module _12_bit_Zero (
  input  [11:0] IN,
  output Out
);

  wire or_1_out, or_2_out, or_3_out, or_4_out, or_5_out, or_6_out, or_7_out, or_8_out, or_9_out, or_10_out,
       or_11_out;

  or or_1 (or_1_out, IN[0], IN[1]);
  or or_2 (or_2_out, or_1_out, IN[2]);
  or or_3 (or_3_out, or_2_out, IN[3]);
  or or_4 (or_4_out, or_3_out, IN[4]);
  or or_5 (or_5_out, or_4_out, IN[5]);
  or or_6 (or_6_out, or_5_out, IN[6]);
  or or_7 (or_7_out, or_6_out, IN[7]);
  or or_8 (or_8_out, or_7_out, IN[8]);
  or or_9 (or_9_out, or_8_out, IN[9]);
  or or_10 (or_10_out, or_9_out, IN[10]);
  or or_11 (or_11_out, or_10_out, IN[11]);
  not not_1 (Out, or_11_out);
endmodule

// Neg
module _12_bit_Negative (
  input  [11:0] Data,
  output N
);


  assign N = Data[11];
endmodule
